# Fritzing sketch UVSensor (saved by Fritzing 0.9.9b)

parts:
  Part3 = Lilypad Arduino Board
  Part4 = Bluetooth HC-05 Macho
  Part5 = GUVA-S12SD UV Light Sensor
  VCC1 = 4 x AAA Battery Mount
  R2 = Resistor [tolerance=±5% power=0.25 resistance=12k package=THT]
  R1 = Resistor [tolerance=±5% power=0.25 resistance=1k package=THT]
  LED1 = smd LED [color="Blue (430nm)" package="0603 [SMD]"]
  LED2 = smd LED [color="Green (555nm)" package="0603 [SMD]"]
  R3 = Resistor [tolerance=±5% power=0.25 resistance=220 package=THT]
  R4 = Resistor [tolerance=±5% power=0.25 resistance=220 package=THT]

nets:
  GND: Part3.GND, Part5.GND, VCC1.-
  N1: Part3.A0, Part5.Out
  N2: Part3.D6, LED1.anode
  N3: Part3.D5, LED2.anode
  N4: Part3.D3, R1.Pin_1
  N5: Part3.D2, Part4.TXD
  VCC: Part3.VCC, Part4.VCC, Part5.5V, VCC1.+
  N6: Part4.GND, R3.Pin_1
  N7: R2.Pin_0, R1.Pin_0
  N8: R2.Pin_1, R4.Pin_1
  N9: LED1.cathode, R3.Pin_0
  N10: LED2.cathode, R4.Pin_0

custom parts:
  GUVA-S12SD UV Light Sensor: Extend your light-sensing spectrum with this analog UV sensor module. It uses a UV photodiode, which can detect the 240-370nm range of light (which covers UVB and most of UVA spectrum). The signal level from the photodiode is very small, in the nano-ampere level, so we tossed on an opamp to amplify the signal to a more manageable volt-level.
